// Digital circuit bit-slice-chips.dig as structural Verilog
module bit_slice_chips (
  input  clk,
  input  in_2,
  input  in_3,
  input  in_4,
  input  in_5,
  output out_6,
  output out_7,
  output out_8,
  output out_9,
  output out_10,
  output out_11,
  output out_12,
  output out_13
);

  wire ADDER_OUT, AND_OUT, CARRY_IN, CARRY_OUT, driver_9_out, driver_25_out, driver_33_out, driver_49_out,
       driver_65_out, driver_81_out, driver_105_out, driver_121_out, DS0_IN, DS0_OUT, DS1_IN, DS1_OUT,
       DS2_IN, DS2_OUT, DS3_IN, DS3_OUT, LOADREG, MUX0_OUT, MUX1_OUT, MUX_OUT, MUXSEL_A, MUXSEL_B, MUXSEL_C,
       MUXSEL_D, NAND_OUT, NOT_OUT, OR_OUT, pulldown_2_out, pulldown_4_out, pulldown_7_out, pulldown_9_out,
       pulldown_11_out, pulldown_13_out, pulldown_14_out, pulldown_16_out, REG_IN0, REG_IN1, REG_IN2,
       REG_IN3, REG_IN4, REG_IN5, REG_IN6, REG_IN7, REG_OUT5, REG_OUT6, REG_OUT7, RESET, STACKDIRSEL, XOR_OUT;
  wire [1:0] dipswitch_1_out, eeprom_1_d;

  DipSwitch dipswitch_1 (.out(dipswitch_1_out[0]));
  DipSwitch dipswitch_2 (.out(dipswitch_1_out[1]));
  DipSwitch dipswitch_3 (.out(REG_IN7));
  DipSwitch dipswitch_4 (.out(REG_IN6));
  DipSwitch dipswitch_5 (.out(REG_IN5));
  Button #(.activeLow("true")) LOAD_IR (.out(LOADREG));
  DipSwitch u_MUXSEL_D (.out(REG_IN3));
  DipSwitch STACK_UP_DOWN (.out(REG_IN4));
  EEPROM #(.Bits(2)) eeprom_1 (.A(dipswitch_1_out), .CS(1'b1), .WE(1'b0), .OE(1'b1), .D(eeprom_1_d));
  DipSwitch u_MUXSEL_C (.out(REG_IN2));
  DipSwitch u_MUXSEL_B (.out(REG_IN1));
  DipSwitch u_MUXSEL_A (.out(REG_IN0));
  LED led_1 (.in(eeprom_1_d[0]));
  LED led_2 (.in(eeprom_1_d[1]));
  Button #(.activeLow("true")) u_RESET (.out(RESET));
  PullDown pulldown_1 (.out(CARRY_IN));
  LED led_3 (.in(DS0_OUT));
  LED led_4 (.in(DS1_OUT));
  LED led_5 (.in(DS2_OUT));
  LED led_6 (.in(DS3_OUT));
  Add add_1 (.a(DS0_OUT), .b(DS1_OUT), .c_i(CARRY_IN), .s(ADDER_OUT), .c_o(CARRY_OUT));
  _7408 AND_gate (
    .pin1(DS0_OUT), .pin2(DS1_OUT), .pin3(AND_OUT), .pin4(1'b0), .pin5(1'b0), .pin7(1'b0), .pin9(1'b0),
    .pin10(1'b0), .pin12(1'b0), .pin13(1'b0), .pin14(1'b1));  // open: pin6, pin8, pin11
  PullUp pullup_1 (.out(RESET));
  _74273 _8_bit_register (
    .pin1(RESET), .pin2(MUXSEL_A), .pin3(REG_IN0), .pin4(REG_IN1), .pin5(MUXSEL_B), .pin6(MUXSEL_C),
    .pin7(REG_IN2), .pin8(REG_IN3), .pin9(MUXSEL_D), .pin10(1'b0), .pin11(LOADREG), .pin12(STACKDIRSEL),
    .pin13(REG_IN4), .pin14(REG_IN5), .pin15(REG_OUT5), .pin16(REG_OUT6), .pin17(REG_IN6), .pin18(REG_IN7),
    .pin19(REG_OUT7), .pin20(1'b1));
  _7400 NAND_gate (
    .pin1(DS0_OUT), .pin2(DS1_OUT), .pin3(NAND_OUT), .pin4(1'b0), .pin5(1'b0), .pin7(1'b0), .pin9(1'b0),
    .pin10(1'b0), .pin12(1'b0), .pin13(1'b0), .pin14(1'b1));  // open: pin6, pin8, pin11
  _7432 OR_gate (
    .pin1(DS0_OUT), .pin2(DS1_OUT), .pin3(OR_OUT), .pin4(1'b0), .pin5(1'b0), .pin7(1'b0), .pin9(1'b0),
    .pin10(1'b0), .pin12(1'b0), .pin13(1'b0), .pin14(1'b1));  // open: pin6, pin8, pin11
  _74151 multiplexer0 (
    .pin1(DS3_OUT), .pin2(DS2_OUT), .pin3(DS1_OUT), .pin4(DS0_OUT), .pin5(MUX0_OUT), .pin7(1'b0),
    .pin8(1'b0), .pin9(MUXSEL_C), .pin10(MUXSEL_B), .pin11(MUXSEL_A), .pin12(in_2), .pin13(NAND_OUT),
    .pin14(ADDER_OUT), .pin15(DS0_OUT), .pin16(1'b1));  // open: pin6
  _74151 multiplexer1 (
    .pin1(XOR_OUT), .pin2(OR_OUT), .pin3(AND_OUT), .pin4(NOT_OUT), .pin5(MUX1_OUT), .pin7(1'b0), .pin8(1'b0),
    .pin9(MUXSEL_C), .pin10(MUXSEL_B), .pin11(MUXSEL_A), .pin12(1'b0), .pin13(DS0_OUT), .pin14(DS0_OUT),
    .pin15(DS0_OUT), .pin16(1'b1));  // open: pin6
  _7486 XOR_gate (
    .pin1(DS0_OUT), .pin2(DS1_OUT), .pin3(XOR_OUT), .pin4(1'b0), .pin5(1'b0), .pin7(1'b0), .pin9(1'b0),
    .pin10(1'b0), .pin12(1'b0), .pin13(1'b0), .pin14(1'b1));  // open: pin6, pin8, pin11
  _74157 multiplexer_select (
    .pin1(MUXSEL_D), .pin2(MUX0_OUT), .pin3(MUX1_OUT), .pin4(MUX_OUT), .pin5(1'b0), .pin6(1'b0), .pin8(1'b0),
    .pin10(1'b0), .pin11(1'b0), .pin13(1'b0), .pin14(1'b0), .pin15(1'b0), .pin16(1'b1));  // open: pin7, pin9, pin12
  _7404 NOT_gate (
    .pin1(DS0_OUT), .pin2(NOT_OUT), .pin3(1'b0), .pin5(1'b0), .pin7(1'b0), .pin9(1'b0), .pin11(1'b0),
    .pin13(1'b0), .pin14(1'b1));  // open: pin4, pin6, pin8, pin10, pin12
  _7474 _1_bit_stack_registers (
    .pin1(RESET), .pin2(DS0_IN), .pin3(clk), .pin4(1'b1), .pin5(DS0_OUT), .pin7(1'b0), .pin9(DS1_OUT),
    .pin10(1'b1), .pin11(clk), .pin12(DS1_IN), .pin13(RESET), .pin14(1'b1));  // open: pin6, pin8
  _7474 _1_bit_stack_registers_2 (
    .pin1(RESET), .pin2(DS2_IN), .pin3(clk), .pin4(1'b1), .pin5(DS2_OUT), .pin7(1'b0), .pin9(DS3_OUT),
    .pin10(1'b1), .pin11(clk), .pin12(DS3_IN), .pin13(RESET), .pin14(1'b1));  // open: pin6, pin8
  _74157 stack_direction_input_select (
    .pin1(STACKDIRSEL), .pin2(MUX_OUT), .pin3(DS1_OUT), .pin4(DS0_IN), .pin5(DS0_OUT), .pin6(DS2_OUT),
    .pin7(DS1_IN), .pin8(1'b0), .pin9(DS2_IN), .pin10(DS3_OUT), .pin11(DS1_OUT), .pin12(DS3_IN),
    .pin13(1'b0), .pin14(DS2_OUT), .pin15(1'b0), .pin16(1'b1));
  _74238 _74238_1 (
    .pin1(in_3), .pin2(in_4), .pin3(in_5), .pin4(1'b0), .pin5(1'b0), .pin6(1'b1), .pin7(out_13), .pin8(1'b0),
    .pin9(out_12), .pin10(out_11), .pin11(out_10), .pin12(out_9), .pin13(out_8), .pin14(out_7),
    .pin15(out_6), .pin16(1'b1));
  PullDown pulldown_2 (.out(pulldown_2_out));
  assign pulldown_2_out = out_6 ? out_6 : 1'bz;  // Driver driver_1
  assign pulldown_2_out = out_7 ? out_7 : 1'bz;  // Driver driver_2
  assign pulldown_2_out = out_8 ? out_8 : 1'bz;  // Driver driver_3
  assign pulldown_2_out = out_9 ? out_9 : 1'bz;  // Driver driver_4
  assign pulldown_2_out = out_10 ? out_10 : 1'bz;  // Driver driver_5
  assign pulldown_2_out = out_11 ? out_11 : 1'bz;  // Driver driver_6
  assign pulldown_2_out = out_12 ? out_12 : 1'bz;  // Driver driver_7
  assign pulldown_2_out = out_13 ? out_13 : 1'bz;  // Driver driver_8
  LED led_7 (.in(pulldown_2_out));
  assign driver_9_out = out_6 ? out_6 : 1'bz;  // Driver driver_9
  assign driver_9_out = out_7 ? out_7 : 1'bz;  // Driver driver_10
  assign driver_9_out = out_8 ? out_8 : 1'bz;  // Driver driver_11
  assign driver_9_out = out_9 ? out_9 : 1'bz;  // Driver driver_12
  assign driver_9_out = out_10 ? out_10 : 1'bz;  // Driver driver_13
  assign driver_9_out = out_11 ? out_11 : 1'bz;  // Driver driver_14
  assign driver_9_out = out_12 ? out_12 : 1'bz;  // Driver driver_15
  assign driver_9_out = out_13 ? out_13 : 1'bz;  // Driver driver_16
  PullDown pulldown_3 (.out(driver_9_out));
  LED led_8 (.in(driver_9_out));
  PullDown pulldown_4 (.out(pulldown_4_out));
  assign pulldown_4_out = out_6 ? out_6 : 1'bz;  // Driver driver_17
  assign pulldown_4_out = out_7 ? out_7 : 1'bz;  // Driver driver_18
  assign pulldown_4_out = out_8 ? out_8 : 1'bz;  // Driver driver_19
  assign pulldown_4_out = out_9 ? out_9 : 1'bz;  // Driver driver_20
  assign pulldown_4_out = out_10 ? out_10 : 1'bz;  // Driver driver_21
  assign pulldown_4_out = out_11 ? out_11 : 1'bz;  // Driver driver_22
  assign pulldown_4_out = out_12 ? out_12 : 1'bz;  // Driver driver_23
  assign pulldown_4_out = out_13 ? out_13 : 1'bz;  // Driver driver_24
  LED led_9 (.in(pulldown_4_out));
  assign driver_25_out = out_6 ? out_6 : 1'bz;  // Driver driver_25
  assign driver_25_out = out_7 ? out_7 : 1'bz;  // Driver driver_26
  assign driver_25_out = out_8 ? out_8 : 1'bz;  // Driver driver_27
  assign driver_25_out = out_9 ? out_9 : 1'bz;  // Driver driver_28
  assign driver_25_out = out_10 ? out_10 : 1'bz;  // Driver driver_29
  assign driver_25_out = out_11 ? out_11 : 1'bz;  // Driver driver_30
  assign driver_25_out = out_12 ? out_12 : 1'bz;  // Driver driver_31
  assign driver_25_out = out_13 ? out_13 : 1'bz;  // Driver driver_32
  PullDown pulldown_5 (.out(driver_25_out));
  LED led_10 (.in(driver_25_out));
  assign driver_33_out = out_6 ? out_6 : 1'bz;  // Driver driver_33
  assign driver_33_out = out_7 ? out_7 : 1'bz;  // Driver driver_34
  assign driver_33_out = out_8 ? out_8 : 1'bz;  // Driver driver_35
  assign driver_33_out = out_9 ? out_9 : 1'bz;  // Driver driver_36
  assign driver_33_out = out_10 ? out_10 : 1'bz;  // Driver driver_37
  assign driver_33_out = out_11 ? out_11 : 1'bz;  // Driver driver_38
  assign driver_33_out = out_12 ? out_12 : 1'bz;  // Driver driver_39
  assign driver_33_out = out_13 ? out_13 : 1'bz;  // Driver driver_40
  PullDown pulldown_6 (.out(driver_33_out));
  LED led_11 (.in(driver_33_out));
  PullDown pulldown_7 (.out(pulldown_7_out));
  assign pulldown_7_out = out_6 ? out_6 : 1'bz;  // Driver driver_41
  assign pulldown_7_out = out_7 ? out_7 : 1'bz;  // Driver driver_42
  assign pulldown_7_out = out_8 ? out_8 : 1'bz;  // Driver driver_43
  assign pulldown_7_out = out_9 ? out_9 : 1'bz;  // Driver driver_44
  assign pulldown_7_out = out_10 ? out_10 : 1'bz;  // Driver driver_45
  assign pulldown_7_out = out_11 ? out_11 : 1'bz;  // Driver driver_46
  assign pulldown_7_out = out_12 ? out_12 : 1'bz;  // Driver driver_47
  assign pulldown_7_out = out_13 ? out_13 : 1'bz;  // Driver driver_48
  LED led_12 (.in(pulldown_7_out));
  assign driver_49_out = out_6 ? out_6 : 1'bz;  // Driver driver_49
  assign driver_49_out = out_7 ? out_7 : 1'bz;  // Driver driver_50
  assign driver_49_out = out_8 ? out_8 : 1'bz;  // Driver driver_51
  assign driver_49_out = out_9 ? out_9 : 1'bz;  // Driver driver_52
  assign driver_49_out = out_10 ? out_10 : 1'bz;  // Driver driver_53
  assign driver_49_out = out_11 ? out_11 : 1'bz;  // Driver driver_54
  assign driver_49_out = out_12 ? out_12 : 1'bz;  // Driver driver_55
  assign driver_49_out = out_13 ? out_13 : 1'bz;  // Driver driver_56
  PullDown pulldown_8 (.out(driver_49_out));
  LED led_13 (.in(driver_49_out));
  PullDown pulldown_9 (.out(pulldown_9_out));
  assign pulldown_9_out = out_6 ? out_6 : 1'bz;  // Driver driver_57
  assign pulldown_9_out = out_7 ? out_7 : 1'bz;  // Driver driver_58
  assign pulldown_9_out = out_8 ? out_8 : 1'bz;  // Driver driver_59
  assign pulldown_9_out = out_9 ? out_9 : 1'bz;  // Driver driver_60
  assign pulldown_9_out = out_10 ? out_10 : 1'bz;  // Driver driver_61
  assign pulldown_9_out = out_11 ? out_11 : 1'bz;  // Driver driver_62
  assign pulldown_9_out = out_12 ? out_12 : 1'bz;  // Driver driver_63
  assign pulldown_9_out = out_13 ? out_13 : 1'bz;  // Driver driver_64
  LED led_14 (.in(pulldown_9_out));
  assign driver_65_out = out_6 ? out_6 : 1'bz;  // Driver driver_65
  assign driver_65_out = out_7 ? out_7 : 1'bz;  // Driver driver_66
  assign driver_65_out = out_8 ? out_8 : 1'bz;  // Driver driver_67
  assign driver_65_out = out_9 ? out_9 : 1'bz;  // Driver driver_68
  assign driver_65_out = out_10 ? out_10 : 1'bz;  // Driver driver_69
  assign driver_65_out = out_11 ? out_11 : 1'bz;  // Driver driver_70
  assign driver_65_out = out_12 ? out_12 : 1'bz;  // Driver driver_71
  assign driver_65_out = out_13 ? out_13 : 1'bz;  // Driver driver_72
  PullDown pulldown_10 (.out(driver_65_out));
  LED led_15 (.in(driver_65_out));
  PullDown pulldown_11 (.out(pulldown_11_out));
  assign pulldown_11_out = out_6 ? out_6 : 1'bz;  // Driver driver_73
  assign pulldown_11_out = out_7 ? out_7 : 1'bz;  // Driver driver_74
  assign pulldown_11_out = out_8 ? out_8 : 1'bz;  // Driver driver_75
  assign pulldown_11_out = out_9 ? out_9 : 1'bz;  // Driver driver_76
  assign pulldown_11_out = out_10 ? out_10 : 1'bz;  // Driver driver_77
  assign pulldown_11_out = out_11 ? out_11 : 1'bz;  // Driver driver_78
  assign pulldown_11_out = out_12 ? out_12 : 1'bz;  // Driver driver_79
  assign pulldown_11_out = out_13 ? out_13 : 1'bz;  // Driver driver_80
  LED led_16 (.in(pulldown_11_out));
  assign driver_81_out = out_6 ? out_6 : 1'bz;  // Driver driver_81
  assign driver_81_out = out_7 ? out_7 : 1'bz;  // Driver driver_82
  assign driver_81_out = out_8 ? out_8 : 1'bz;  // Driver driver_83
  assign driver_81_out = out_9 ? out_9 : 1'bz;  // Driver driver_84
  assign driver_81_out = out_10 ? out_10 : 1'bz;  // Driver driver_85
  assign driver_81_out = out_11 ? out_11 : 1'bz;  // Driver driver_86
  assign driver_81_out = out_12 ? out_12 : 1'bz;  // Driver driver_87
  assign driver_81_out = out_13 ? out_13 : 1'bz;  // Driver driver_88
  PullDown pulldown_12 (.out(driver_81_out));
  LED led_17 (.in(driver_81_out));
  PullDown pulldown_13 (.out(pulldown_13_out));
  assign pulldown_13_out = out_6 ? out_6 : 1'bz;  // Driver driver_89
  assign pulldown_13_out = out_7 ? out_7 : 1'bz;  // Driver driver_90
  assign pulldown_13_out = out_8 ? out_8 : 1'bz;  // Driver driver_91
  assign pulldown_13_out = out_9 ? out_9 : 1'bz;  // Driver driver_92
  assign pulldown_13_out = out_10 ? out_10 : 1'bz;  // Driver driver_93
  assign pulldown_13_out = out_11 ? out_11 : 1'bz;  // Driver driver_94
  assign pulldown_13_out = out_12 ? out_12 : 1'bz;  // Driver driver_95
  assign pulldown_13_out = out_13 ? out_13 : 1'bz;  // Driver driver_96
  LED led_18 (.in(pulldown_13_out));
  PullDown pulldown_14 (.out(pulldown_14_out));
  assign pulldown_14_out = out_6 ? out_6 : 1'bz;  // Driver driver_97
  assign pulldown_14_out = out_7 ? out_7 : 1'bz;  // Driver driver_98
  assign pulldown_14_out = out_8 ? out_8 : 1'bz;  // Driver driver_99
  assign pulldown_14_out = out_9 ? out_9 : 1'bz;  // Driver driver_100
  assign pulldown_14_out = out_10 ? out_10 : 1'bz;  // Driver driver_101
  assign pulldown_14_out = out_11 ? out_11 : 1'bz;  // Driver driver_102
  assign pulldown_14_out = out_12 ? out_12 : 1'bz;  // Driver driver_103
  assign pulldown_14_out = out_13 ? out_13 : 1'bz;  // Driver driver_104
  LED led_19 (.in(pulldown_14_out));
  assign driver_105_out = out_6 ? out_6 : 1'bz;  // Driver driver_105
  assign driver_105_out = out_7 ? out_7 : 1'bz;  // Driver driver_106
  assign driver_105_out = out_8 ? out_8 : 1'bz;  // Driver driver_107
  assign driver_105_out = out_9 ? out_9 : 1'bz;  // Driver driver_108
  assign driver_105_out = out_10 ? out_10 : 1'bz;  // Driver driver_109
  assign driver_105_out = out_11 ? out_11 : 1'bz;  // Driver driver_110
  assign driver_105_out = out_12 ? out_12 : 1'bz;  // Driver driver_111
  assign driver_105_out = out_13 ? out_13 : 1'bz;  // Driver driver_112
  PullDown pulldown_15 (.out(driver_105_out));
  LED led_20 (.in(driver_105_out));
  PullDown pulldown_16 (.out(pulldown_16_out));
  assign pulldown_16_out = out_6 ? out_6 : 1'bz;  // Driver driver_113
  assign pulldown_16_out = out_7 ? out_7 : 1'bz;  // Driver driver_114
  assign pulldown_16_out = out_8 ? out_8 : 1'bz;  // Driver driver_115
  assign pulldown_16_out = out_9 ? out_9 : 1'bz;  // Driver driver_116
  assign pulldown_16_out = out_10 ? out_10 : 1'bz;  // Driver driver_117
  assign pulldown_16_out = out_11 ? out_11 : 1'bz;  // Driver driver_118
  assign pulldown_16_out = out_12 ? out_12 : 1'bz;  // Driver driver_119
  assign pulldown_16_out = out_13 ? out_13 : 1'bz;  // Driver driver_120
  LED led_21 (.in(pulldown_16_out));
  assign driver_121_out = out_6 ? out_6 : 1'bz;  // Driver driver_121
  assign driver_121_out = out_7 ? out_7 : 1'bz;  // Driver driver_122
  assign driver_121_out = out_8 ? out_8 : 1'bz;  // Driver driver_123
  assign driver_121_out = out_9 ? out_9 : 1'bz;  // Driver driver_124
  assign driver_121_out = out_10 ? out_10 : 1'bz;  // Driver driver_125
  assign driver_121_out = out_11 ? out_11 : 1'bz;  // Driver driver_126
  assign driver_121_out = out_12 ? out_12 : 1'bz;  // Driver driver_127
  assign driver_121_out = out_13 ? out_13 : 1'bz;  // Driver driver_128
  PullDown pulldown_17 (.out(driver_121_out));
  LED led_22 (.in(driver_121_out));

  // Other names for the same wires on the sheet: CLK_DS0 = clk; CLK_DS1 = clk; CLK_DS2 = clk; CLK_DS3 = clk;
  //   DATABUS = in_2; LEFTBIT_0 = DS0_OUT; LEFTBIT_LSB = DS0_OUT; RIGHTBIT_0 = DS0_OUT; RIGHTBIT_MSB = DS0_OUT

  // Notes on the sheet:
  //   contents of eeprom_1 (hex, n*v repeats v):
  //   0,1,a,3
  //   Clock
  //   Logic
  //   Instruction Register
  //   Connected due to 1-bit
  //   Plexing
  //   Data Stack
endmodule
